// Logisim project BeEight.circ as structural Verilog: 3 circuits, main circuit main
module main (
  input  D0,
  input  RESET,
  input  D1,
  input  HLT,
  input  D2,
  input  RES,
  input  D3,
  output [11:0] Address
);

  wire AD0, AD1, AD2, AD3, AD4, AD5, AD6, AD7, adder_2_cout, and_1_out, and_2_out, and_3_out, and_4_out,
       and_6_out, and_7_out, and_8_out, and_12_out, and_13_out, Carry, CLK, CLKIN, ConditionalFlag,
       ConditionalResult, controlled_buffer_14_out, controlled_buffer_15_out, controlled_buffer_16_out,
       controlled_buffer_17_out, controlled_buffer_18_out, controlled_buffer_19_out,
       controlled_buffer_21_out, controlled_buffer_22_out, controlled_buffer_23_out, Equal, GreaterThan, ia,
       ialu, im, ipb, ipc, ipcs, isb, LessThan, n74138_1_pin4, n74138_1_pin5, n74138_1_pin6, n74138_1_pin7,
       n74138_1_pin9, n74138_1_pin10, n74138_1_pin11, n74138_1_pin12, n74138_1_pin13, n74138_1_pin14,
       n74138_1_pin15, nand_2_out, nor_1_out, not_1_out, not_2_out, not_3_out, not_4_out, not_5_out,
       not_6_out, not_7_out, not_8_out, not_9_out, not_10_out, not_11_out, not_12_out, not_13_out,
       not_14_out, not_16_out, not_17_out, not_18_out, not_19_out, not_20_out, nxt, oa, oalu, om, opb, opc,
       opcs, or_1_out, or_2_out, or_3_out, osb, pull_resistor_2_node, pull_resistor_3_node, s_r_ff_1_qn,
       special, ucf;
  wire [3:0] Condition, controlled_buffer_4_out, DatabusUpper, Instruction, InstructionCounter,
       pull_resistor_1_node;
  wire [6:0] rom_1_data;
  wire [7:0] Accumulator, adder_1_out, adder_2_out, ALU, ALUbuffer_q, ALUin, nand_1_out, not_15_out,
       PrimaryBuffer, ProgramCounterStorageLower_q, ProgramCounterStorageUpper_q, SecondaryBuffer,
       SecondaryBuffer_q;
  wire [11:0] StoredAddress;

  Hex_Digit_Display #(.decimalPoint("false")) hex_digit_display_1 (.value(Instruction));
  Pull_Resistor pull_resistor_1 (.node(pull_resistor_1_node));
  and and_1 (and_1_out, osb, Instruction[0], Instruction[1], Instruction[2]);
  Hex_Digit_Display #(.decimalPoint("false")) hex_digit_display_2 (.value(Address[11:8]));
  Hex_Digit_Display #(.decimalPoint("false")) hex_digit_display_3 (.value(Address[7:4]));
  Hex_Digit_Display #(.decimalPoint("false")) hex_digit_display_4 (.value(InstructionCounter));
  not not_1 (not_1_out, and_1_out);
  and and_2 (and_2_out, and_1_out, ConditionalFlag);
  Hex_Digit_Display #(.decimalPoint("false")) hex_digit_display_5 (.value(Address[3:0]));
  Hex_Digit_Display #(.decimalPoint("false")) hex_digit_display_6 (.value(DatabusUpper));
  Hex_Digit_Display #(.decimalPoint("false")) hex_digit_display_7 (.value({AD7, AD6, AD5, AD4}));
  Register ProgramCounterStorageLower (
    .D({AD7, AD6, AD5, AD4, AD3, AD2, AD1, AD0}), .en(ipcs), .clk(CLK), .Q(ProgramCounterStorageLower_q),
    .clr(RESET));
  Register ProgramCounterStorageUpper (
    .D({pull_resistor_1_node, DatabusUpper}), .en(ipcs), .clk(CLK), .Q(ProgramCounterStorageUpper_q),
    .clr(RESET));
  or or_1 (or_1_out, not_1_out, and_2_out);
  Hex_Digit_Display #(.decimalPoint("false")) hex_digit_display_8 (.value(Accumulator[7:4]));
  Hex_Digit_Display #(.decimalPoint("false")) hex_digit_display_9 (.value(Accumulator[3:0]));
  Hex_Digit_Display #(.decimalPoint("false")) hex_digit_display_10 (.value({AD3, AD2, AD1, AD0}));
  Hex_Digit_Display #(.decimalPoint("false")) hex_digit_display_11 (.value(PrimaryBuffer[7:4]));
  RAM #(.addrWidth(12), .databus("bidir"), .trigger("high"), .\type ("nonvolatile")) ram_1 (
    .addr(Address), .we(im), .oe(om), .data({AD7, AD6, AD5, AD4, AD3, AD2, AD1, AD0}));
  and and_3 (and_3_out, CLK, or_1_out, ipc);
  Hex_Digit_Display #(.decimalPoint("false")) hex_digit_display_12 (.value(ALU[7:4]));
  Hex_Digit_Display #(.decimalPoint("false")) hex_digit_display_13 (.value(ALU[3:0]));
  Hex_Digit_Display #(.decimalPoint("false")) hex_digit_display_14 (.value(PrimaryBuffer[3:0]));
  Hex_Digit_Display #(.decimalPoint("false")) hex_digit_display_15 (.value(SecondaryBuffer[7:4]));
  Clock u_CLK (.out(CLKIN));
  assign {AD7, AD6, AD5, AD4, AD3, AD2, AD1, AD0} = and_4_out ? ProgramCounterStorageLower_q : 8'bz;  // Controlled_Buffer controlled_buffer_1
  and and_4 (and_4_out, opcs, not_2_out);
  not not_2 (not_2_out, special);
  assign DatabusUpper = opcs ? ProgramCounterStorageUpper_q[3:0] : 4'bz;  // Controlled_Buffer controlled_buffer_2
  Counter #(.max('hfff), .width(12)) ProgramCounter (
    .clr(RESET), .load(not_3_out), .up(1'b1), .count(special), .clk(and_3_out),
    .D({DatabusUpper, AD7, AD6, AD5, AD4, AD3, AD2, AD1, AD0}), .Q(Address));  // open: carry
  not not_3 (not_3_out, special);
  LED led_1 (.in(om));
  LED led_2 (.in(im));
  Hex_Digit_Display #(.decimalPoint("false")) hex_digit_display_16 (.value(SecondaryBuffer[3:0]));
  LED led_3 (.in(opb));
  LED led_4 (.in(osb));
  LED led_5 (.in(ipb));
  LED led_6 (.in(isb));
  Hex_Digit_Display #(.decimalPoint("false")) hex_digit_display_17 (.value(StoredAddress[11:8]));
  Hex_Digit_Display #(.decimalPoint("false")) hex_digit_display_18 (.value(StoredAddress[7:4]));
  LED led_7 (.in(oa));
  LED led_8 (.in(oalu));
  LED led_9 (.in(ia));
  LED led_10 (.in(ialu));
  Hex_Digit_Display #(.decimalPoint("false")) hex_digit_display_19 (.value(StoredAddress[3:0]));
  assign {DatabusUpper, AD7, AD6, AD5, AD4, AD3, AD2, AD1, AD0} = opc ? Address : 12'bz;  // Controlled_Buffer controlled_buffer_3
  LED led_11 (.in(opc));
  LED led_12 (.in(opcs));
  LED led_13 (.in(ipc));
  LED led_14 (.in(ipcs));
  LED led_15 (.in(special));
  LED led_16 (.in(CLK));
  LED led_17 (.in(nxt));
  LED led_18 (.in(ConditionalFlag));
  LED RD (.in(om));
  LED WR (.in(im));
  S_R_Flip_Flop s_r_ff_1 (.reset(RES), .Qn(s_r_ff_1_qn), .preset(HLT));  // open: S, R, clk, Q
  and and_5 (CLK, s_r_ff_1_qn, CLKIN);
  or or_2 (or_2_out, RESET, nxt);
  ROM rom_1 (.addr({Instruction, InstructionCounter}), .data({nxt, rom_1_data[6:4], special, rom_1_data[2:0]}));
  assign controlled_buffer_4_out = special ? Instruction : 4'bz;  // Controlled_Buffer controlled_buffer_4
  not not_4 (not_4_out, special);
  assign controlled_buffer_4_out = not_4_out ? {AD7, AD6, AD5, AD4} : 4'bz;  // Controlled_Buffer controlled_buffer_5
  Counter #(.max('hf), .trigger("falling"), .width(4)) counter_1 (
    .clr(or_2_out), .load(1'b0), .up(1'b1), .count(1'b1), .clk(CLK), .Q(InstructionCounter));  // open: D, carry
  Register u_PrimaryBuffer (
    .D({controlled_buffer_4_out, AD3, AD2, AD1, AD0}), .en(ipb), .clk(CLK), .Q({Instruction, Condition}));  // open: clr
  Register u_SecondaryBuffer (
    .D({AD7, AD6, AD5, AD4, AD3, AD2, AD1, AD0}), .en(isb), .clk(CLK), .Q(SecondaryBuffer_q));  // open: clr
  assign DatabusUpper = osb ? Condition : 4'bz;  // Controlled_Buffer controlled_buffer_6
  Adder adder_1 (
    .a(Accumulator), .b({AD7, AD6, AD5, AD4, AD3, AD2, AD1, AD0}), .out(adder_1_out), .cin(ConditionalFlag),
    .cout(Carry));
  assign nand_1_out = ~(Accumulator & {AD7, AD6, AD5, AD4, AD3, AD2, AD1, AD0});  // NAND_Gate nand_1, 8 bits wide
  assign {AD7, AD6, AD5, AD4, AD3, AD2, AD1, AD0} = osb ? SecondaryBuffer_q : 8'bz;  // Controlled_Buffer controlled_buffer_7
  not not_5 (not_5_out, Instruction[3]);
  not not_6 (not_6_out, Condition[0]);
  and and_6 (and_6_out, not_5_out, Condition[0], Instruction[0]);
  and and_7 (and_7_out, not_5_out, not_6_out, Instruction[0]);
  assign ALUin = and_7_out ? {Accumulator[6:0], ConditionalFlag} : 8'bz;  // Controlled_Buffer controlled_buffer_8
  assign ALUin = and_6_out ? {ConditionalFlag, Accumulator[7:1]} : 8'bz;  // Controlled_Buffer controlled_buffer_9
  and and_8 (and_8_out, Instruction[3], Instruction[0]);
  not not_7 (not_7_out, Instruction[0]);
  assign ALUin = not_7_out ? adder_1_out : 8'bz;  // Controlled_Buffer controlled_buffer_10
  assign ALUin = and_8_out ? nand_1_out : 8'bz;  // Controlled_Buffer controlled_buffer_11
  Demultiplexer #(.select(3)) demultiplexer_1 (
    .out1(im), .out2(ipb), .out3(isb), .out4(ia), .out5(ialu), .out6(ipc), .out7(ipcs), .in(1'b1),
    .sel(rom_1_data[2:0]));  // open: out0
  Demultiplexer #(.select(3)) demultiplexer_2 (
    .out1(om), .out2(opb), .out3(osb), .out4(oa), .out5(oalu), .out6(opc), .out7(opcs), .in(1'b1),
    .sel(rom_1_data[6:4]));  // open: out0
  Register ALUbuffer (.D(ALUin), .en(ialu), .clk(CLK), .Q(ALUbuffer_q));  // open: clr
  OctalDTypeLatchOE octaldtypelatchoe_1 (
    .D0(AD0), .D1(AD1), .D2(AD2), .D3(AD3), .D4(AD4), .D5(AD5), .D6(AD6), .CK(nand_2_out), .nOE(1'b0),
    .D7(AD7), .Q0(Accumulator[0]), .Q1(Accumulator[1]), .Q2(Accumulator[2]), .Q3(Accumulator[3]),
    .Q4(Accumulator[4]), .Q5(Accumulator[5]), .Q6(Accumulator[6]), .Q7(Accumulator[7]));
  assign {AD7, AD6, AD5, AD4, AD3, AD2, AD1, AD0} = oalu ? ALUbuffer_q : 8'bz;  // Controlled_Buffer controlled_buffer_12
  nand nand_2 (nand_2_out, CLK, ia);
  and and_9 (ucf, ialu, special);
  assign {AD7, AD6, AD5, AD4, AD3, AD2, AD1, AD0} = oa ? Accumulator : 8'bz;  // Controlled_Buffer controlled_buffer_13
  _74138 #(.ShowInternalStructure("true")) u_74138_1 (
    .pin1(Condition[1]), .pin2(Condition[2]), .pin3(Condition[3]), .pin4(n74138_1_pin4),
    .pin5(n74138_1_pin5), .pin6(n74138_1_pin6), .pin7(n74138_1_pin7), .pin15(n74138_1_pin15),
    .pin14(n74138_1_pin14), .pin13(n74138_1_pin13), .pin12(n74138_1_pin12), .pin11(n74138_1_pin11),
    .pin10(n74138_1_pin10), .pin9(n74138_1_pin9));
  not not_8 (not_8_out, n74138_1_pin15);
  Pull_Resistor pull_resistor_2 (.node(pull_resistor_2_node));
  assign controlled_buffer_14_out = not_8_out ? pull_resistor_2_node : 1'bz;  // Controlled_Buffer controlled_buffer_14
  not not_9 (not_9_out, n74138_1_pin14);
  not not_10 (not_10_out, ucf);
  assign controlled_buffer_15_out = not_9_out ? Equal : 1'bz;  // Controlled_Buffer controlled_buffer_15
  not not_11 (not_11_out, n74138_1_pin13);
  assign controlled_buffer_16_out = not_11_out ? LessThan : 1'bz;  // Controlled_Buffer controlled_buffer_16
  not not_12 (not_12_out, n74138_1_pin12);
  assign controlled_buffer_17_out = not_12_out ? GreaterThan : 1'bz;  // Controlled_Buffer controlled_buffer_17
  not not_13 (not_13_out, n74138_1_pin11);
  assign controlled_buffer_18_out = not_13_out ? D0 : 1'bz;  // Controlled_Buffer controlled_buffer_18
  not not_14 (not_14_out, n74138_1_pin10);
  assign not_15_out = ~Accumulator;  // NOT_Gate not_15, 8 bits wide
  assign controlled_buffer_19_out = not_10_out ? Carry : 1'bz;  // Controlled_Buffer controlled_buffer_19
  assign controlled_buffer_19_out = ucf ? ConditionalResult : 1'bz;  // Controlled_Buffer controlled_buffer_20
  assign controlled_buffer_21_out = not_14_out ? D1 : 1'bz;  // Controlled_Buffer controlled_buffer_21
  not not_16 (not_16_out, n74138_1_pin9);
  assign controlled_buffer_22_out = not_16_out ? D2 : 1'bz;  // Controlled_Buffer controlled_buffer_22
  not not_17 (not_17_out, n74138_1_pin7);
  assign controlled_buffer_23_out = not_17_out ? D3 : 1'bz;  // Controlled_Buffer controlled_buffer_23
  Pull_Resistor #(.pull(1)) pull_resistor_3 (.node(pull_resistor_3_node));
  Adder adder_2 (
    .a({AD7, AD6, AD5, AD4, AD3, AD2, AD1, AD0}), .b(not_15_out), .out(adder_2_out),
    .cin(pull_resistor_3_node), .cout(adder_2_cout));
  Register #(.width(1)) register_1 (
    .D(controlled_buffer_19_out), .en(ialu), .clk(CLK), .Q(ConditionalFlag));  // open: clr
  Pull_Resistor pull_resistor_4 (.node(controlled_buffer_14_out));
  Pull_Resistor pull_resistor_5 (.node(controlled_buffer_15_out));
  Pull_Resistor pull_resistor_6 (.node(controlled_buffer_16_out));
  Pull_Resistor pull_resistor_7 (.node(controlled_buffer_17_out));
  Pull_Resistor pull_resistor_8 (.node(controlled_buffer_18_out));
  Pull_Resistor pull_resistor_9 (.node(controlled_buffer_21_out));
  Pull_Resistor pull_resistor_10 (.node(controlled_buffer_22_out));
  Pull_Resistor pull_resistor_11 (.node(controlled_buffer_23_out));
  nor nor_1 (nor_1_out, adder_2_out[0], adder_2_out[1], adder_2_out[2], adder_2_out[3], adder_2_out[4], adder_2_out[5], adder_2_out[6], adder_2_out[7]);
  not not_18 (not_18_out, nor_1_out);
  and and_10 (Equal, nor_1_out, adder_2_cout);
  and and_11 (LessThan, adder_2_cout, not_18_out);
  nor nor_2 (GreaterThan, Equal, LessThan);
  or or_3 (or_3_out, controlled_buffer_14_out, controlled_buffer_15_out, controlled_buffer_16_out, controlled_buffer_17_out, controlled_buffer_18_out, controlled_buffer_21_out, controlled_buffer_22_out, controlled_buffer_23_out);
  not not_19 (not_19_out, or_3_out);
  assign ConditionalResult = and_12_out ? or_3_out : 1'bz;  // Controlled_Buffer controlled_buffer_24
  and and_12 (and_12_out, ucf, not_20_out);
  and and_13 (and_13_out, ucf, Condition[0]);
  assign ConditionalResult = and_13_out ? not_19_out : 1'bz;  // Controlled_Buffer controlled_buffer_25
  Pull_Resistor pull_resistor_12 (.node(ConditionalResult));
  not not_20 (not_20_out, Condition[0]);
  // also tied to GND on the sheet: {n74138_1_pin4, n74138_1_pin5}
  // also tied to VCC on the sheet: n74138_1_pin6

  // Other names for the same wires on the sheet: Databus[7:0] = {AD7, AD6, AD5, AD4, AD3, AD2, AD1, AD0};
  //   Memory[7:0] = {AD7, AD6, AD5, AD4, AD3, AD2, AD1, AD0}; AQ0 = Accumulator[0]; AQ1 = Accumulator[1];
  //   AQ2 = Accumulator[2]; AQ3 = Accumulator[3]; AQ4 = Accumulator[4]; AQ5 = Accumulator[5]; AQ6 = Accumulator[6];
  //   AQ7 = Accumulator[7]; Dev0 = D0; Dev1 = D1; Dev2 = D2; Dev3 = D3; HALT = HLT

  // Notes on the sheet:
  //   SL
  //   SR
  //   contents of rom_1 (hex, n*v repeats v):
  //   12 e 14 e 80 11*0 12 e 80 13*0 12 e 13 e 35 54 80 9*0 12 e 5 54 80 11*0 12 e 1d e 80 11*0 12 e 80
  //   13*0 12 e 13 36 80 11*0 12 e 13 e 36 80 10*0 12 e 13 e 67 36 14 76 80 7*0 12 e 13 e 67 36 41 76 80
  //   7*0 12 e 13 e 67 36 13 35 54 76 80 5*0 12 e 13 e 13 35 54 80 8*0 12 5d e 80 12*0 12 e 13 e 67 36 79
  //   e 71 76 80 5*0 12 e 13 36 1a e 13 36 80 7*0 12 e 13 36 1a e 13 36 80
  //   This is basically a Multiplexer
endmodule

module OctalDTypeLatchOE (
  input  D0,
  input  D1,
  input  D2,
  input  D3,
  input  D4,
  input  D5,
  input  D6,
  input  D7,
  input  CK,
  input  nOE,
  output Q0,
  output Q1,
  output Q2,
  output Q3,
  output Q4,
  output Q5,
  output Q6,
  output Q7
);

  wire d_ff_1_qn, d_ff_2_qn, d_ff_3_qn, d_ff_4_qn, d_ff_5_qn, d_ff_6_qn, d_ff_7_qn, d_ff_8_qn, not_1_out,
       not_2_out, not_3_out;

  D_Flip_Flop d_ff_1 (.D(D0), .clk(not_2_out), .Qn(d_ff_1_qn));  // open: Q, preset, reset
  not not_1 (not_1_out, CK);
  not not_2 (not_2_out, not_1_out);
  not not_3 (not_3_out, nOE);
  D_Flip_Flop d_ff_2 (.D(D1), .clk(not_2_out), .Qn(d_ff_2_qn));  // open: Q, preset, reset
  assign Q0 = not_3_out ? ~d_ff_1_qn : 1'bz;  // Controlled_Inverter controlled_inverter_1
  D_Flip_Flop d_ff_3 (.D(D2), .clk(not_2_out), .Qn(d_ff_3_qn));  // open: Q, preset, reset
  assign Q1 = not_3_out ? ~d_ff_2_qn : 1'bz;  // Controlled_Inverter controlled_inverter_2
  D_Flip_Flop d_ff_4 (.D(D3), .clk(not_2_out), .Qn(d_ff_4_qn));  // open: Q, preset, reset
  assign Q2 = not_3_out ? ~d_ff_3_qn : 1'bz;  // Controlled_Inverter controlled_inverter_3
  D_Flip_Flop d_ff_5 (.D(D4), .clk(not_2_out), .Qn(d_ff_5_qn));  // open: Q, preset, reset
  assign Q3 = not_3_out ? ~d_ff_4_qn : 1'bz;  // Controlled_Inverter controlled_inverter_4
  D_Flip_Flop d_ff_6 (.D(D5), .clk(not_2_out), .Qn(d_ff_6_qn));  // open: Q, preset, reset
  assign Q4 = not_3_out ? ~d_ff_5_qn : 1'bz;  // Controlled_Inverter controlled_inverter_5
  D_Flip_Flop d_ff_7 (.D(D6), .clk(not_2_out), .Qn(d_ff_7_qn));  // open: Q, preset, reset
  assign Q5 = not_3_out ? ~d_ff_6_qn : 1'bz;  // Controlled_Inverter controlled_inverter_6
  D_Flip_Flop d_ff_8 (.D(D7), .clk(not_2_out), .Qn(d_ff_8_qn));  // open: Q, preset, reset
  assign Q6 = not_3_out ? ~d_ff_7_qn : 1'bz;  // Controlled_Inverter controlled_inverter_7
  assign Q7 = not_3_out ? ~d_ff_8_qn : 1'bz;  // Controlled_Inverter controlled_inverter_8
endmodule

module extTest (
);

  main main_1 ();  // open: D0, RESET, D1, HLT, D2, RES, D3, Address
endmodule
